# Fritzing sketch TankLevel (saved by Fritzing 0.9.9b)
circuit board: 15cm x 11cm
breadboards: 2

parts:
  PIC_16F877A1 = PIC 16F877A [package=THT]
  LCD1 = LCD screen
  R1 = Resistor [tolerance=±1% power=0.25 resistance=330 package=THT]
  U1 = POT [package=pot_alpha_rv16af-20]
  HC-SR04_Sensor_1 = HC-SR04 Ultrasonic Distance Sensor
  HC-SR04_Sensor_2 = HC-SR04 Ultrasonic Distance Sensor
  HC-SR04_Sensor_3 = HC-SR04 Ultrasonic Distance Sensor
  HC-SR04_Sensor_4 = HC-SR04 Ultrasonic Distance Sensor
  C1 = Capacitor [package=cap-pth-small2]
  C2 = Capacitor [package=cap-pth-small2]
  IC2 = IC, DIP package, 16 pins [chip_label=HEF4539B]
  C3 = Capacitor [package=cap-pth-small-kit]
  C4 = Capacitor [package=cap-pth-small-kit]
  J1 = Power Jack [package=power_jack_pth]
  VCC1 = 4 x AAA Battery Mount
  S1 = SPST Switch [package=switch-spdt_lock.007s]
  R2 = Resistor [tolerance=±5% power=0.25 resistance=1k package=THT]
  R3 = Resistor [tolerance=±5% power=0.25 resistance=1k package=THT]
  R4 = Resistor [tolerance=±5% power=0.25 resistance=1k package=THT]
  R5 = Resistor [tolerance=±5% power=0.25 resistance=1k package=THT]
  XTAL1 = Crystal [frequency="4 MHz" package=THT]
  KP7 = Header 1 [package=1x01_offset]
  KP6 = Header 1 [package=1x01_offset]
  KP5 = Header 1 [package=1x01_offset]
  KP4 = Header 1 [package=1x01_offset]
  KP3 = Header 1 [package=1x01_offset]
  KP2 = Header 1 [package=1x01_offset]
  KP1 = Header 1 [package=1x01_offset]
  JP10 = Header 1 [package=1x01_offset]
  JP11 = Header 1 [package=1x01_offset]
  JP12 = Header 1 [package=1x01_offset]
  JP13 = Header 1 [package=1x01_offset]
  JP14 = Header 1 [package=1x01_offset]
  JP15 = Header 1 [package=1x01_offset]
  JP16 = Header 1 [package=1x01_offset]
  JP17 = Header 1 [package=1x01_offset]
  JP18 = Header 1 [package=1x01_offset]
  JP19 = Header 1 [package=1x01_offset]
  JP20 = Header 1 [package=1x01_offset]
  JP21 = Header 1 [package=1x01_offset]
  JP22 = Header 1 [package=1x01_offset]
  JP23 = Header 1 [package=1x01_offset]
  JP24 = Header 1 [package=1x01_offset]
  JP25 = Header 1 [package=1x01_offset]
  JP26 = Header 1 [package=1x01_offset]
  JP27 = Header 1 [package=1x01_offset]
  JP28 = Header 1 [package=1x01_offset]
  JP29 = Header 1 [package=1x01_offset]
  JP30 = Header 1 [package=1x01_offset]
  JP31 = Header 1 [package=1x01_offset]
  U2 = Voltage Regulator - 5V [package="TO220 [THT]"]
  IC1 = IC, DIP package, 16 pins [chip_label=74HC139]

nets:
  VCC: PIC_16F877A1.MCLR, PIC_16F877A1.VDD, LCD1.VDD, R1.Pin_1, U1.E, HC-SR04_Sensor_1.VCC, HC-SR04_Sensor_2.VCC, HC-SR04_Sensor_3.VCC, HC-SR04_Sensor_4.VCC, IC2.pin16, C3.1, JP12.1, JP13.1, JP14.1, JP15.1, JP16.1, JP17.1, JP18.1, JP19.1, JP20.1, JP21.1, JP22.1, JP23.1, U2.output_voltage, IC1.pin16
  N1: PIC_16F877A1.RA0/AN0, IC2.pin7, JP10.1, JP11.1
  N2: PIC_16F877A1.RA1/AN1, IC2.pin15, IC1.pin2
  N3: PIC_16F877A1.RA2/AN2, IC2.pin2, IC1.pin3
  N4: PIC_16F877A1.RA3/AN3, IC1.pin1
  GND: PIC_16F877A1.VSS, LCD1.VSS, LCD1.LED-, U1.A, HC-SR04_Sensor_1.GND, HC-SR04_Sensor_2.GND, HC-SR04_Sensor_3.GND, HC-SR04_Sensor_4.GND, C1.2, C2.1, IC2.pin1, IC2.pin8, C3.2, C4.1, J1.GND, R2.Pin_1, R3.Pin_0, R4.Pin_0, R5.Pin_0, JP24.1, JP25.1, JP26.1, JP27.1, JP28.1, JP29.1, JP30.1, JP31.1, U2.GND, IC1.pin8
  N5: PIC_16F877A1.OSC1/CLKIN, C2.2, XTAL1.pin_1
  N6: PIC_16F877A1.OSC2/CLKOUT, C1.1, XTAL1.pin_0
  N7: PIC_16F877A1.RC0, R3.Pin_1, KP1.1
  N8: PIC_16F877A1.RC1, R4.Pin_1, KP2.1
  N9: PIC_16F877A1.RC2, KP3.1
  N10: PIC_16F877A1.RC3, R5.Pin_1, KP4.1
  N11: PIC_16F877A1.RC4, KP5.1
  N12: PIC_16F877A1.RC5, R2.Pin_0, KP6.1
  N13: PIC_16F877A1.RC6/TX/CK, KP7.1
  N14: PIC_16F877A1.RD5/PSP5, LCD1.RS
  N15: PIC_16F877A1.RD6/PSP6, LCD1.R/W
  N16: PIC_16F877A1.RD7/PSP7, LCD1.E
  N17: PIC_16F877A1.RB0/INT, LCD1.DB0
  N18: PIC_16F877A1.RB1, LCD1.DB1
  N19: PIC_16F877A1.RB2, LCD1.DB2
  N20: PIC_16F877A1.RB3, LCD1.DB3
  N21: PIC_16F877A1.RB4, LCD1.DB4
  N22: PIC_16F877A1.RB5, LCD1.DB5
  N23: PIC_16F877A1.RB6, LCD1.DB6
  N24: PIC_16F877A1.RB7, LCD1.DB7
  N25: LCD1.V0, U1.S
  N26: LCD1.LED+, R1.Pin_0
  N27: HC-SR04_Sensor_1.TRIG, IC1.pin4
  N28: HC-SR04_Sensor_1.ECHO, IC2.pin6
  N29: HC-SR04_Sensor_2.TRIG, IC1.pin5
  N30: HC-SR04_Sensor_2.ECHO, IC2.pin5
  N31: HC-SR04_Sensor_3.TRIG, IC1.pin6
  N32: HC-SR04_Sensor_3.ECHO, IC2.pin4
  N33: HC-SR04_Sensor_4.TRIG, IC1.pin7
  N34: HC-SR04_Sensor_4.ECHO, IC2.pin3
  N35: C4.2, S1.P, U2.input_voltage
  N36: J1.GNDBREAK, VCC1.-
  N37: J1.PWR, VCC1.+, S1.O
